# Fritzing sketch duino-motor-driver-lc (saved by Fritzing 0.9.3b)
breadboards: 1

parts:
  M1 = DC Motor
  M2 = DC Motor
  Power_plug1 = Power plug
  Dual_MC33926_Motor_Driver_Carrier1 = Pololu #1213 Dual MC33926 Motor Driver Carrier [package=THT]
  Teensy_3_1 = Teensy 3.1
  Raspberry_Pi_Zero1 = Raspberry Pi Zero
  R2 = Resistor [tolerance=±5% resistance=4.7k package=THT]
  R1 = Resistor [tolerance=±5% resistance=4.7k package=THT]

nets:
  N1: M1.pin_1, Dual_MC33926_Motor_Driver_Carrier1.M1_OUT2
  N2: M1.pin_2, Dual_MC33926_Motor_Driver_Carrier1.M1_OUT1
  N3: M2.pin_1, Dual_MC33926_Motor_Driver_Carrier1.M2_OUT2
  N4: M2.pin_2, Dual_MC33926_Motor_Driver_Carrier1.M2_OUT1
  GND: Power_plug1.GND, Dual_MC33926_Motor_Driver_Carrier1.GND, Dual_MC33926_Motor_Driver_Carrier1.M1_PWM_D1, Dual_MC33926_Motor_Driver_Carrier1.M2_PWM_D1, Dual_MC33926_Motor_Driver_Carrier1.JP2, Dual_MC33926_Motor_Driver_Carrier1.JP8, Teensy_3_1.GND, Raspberry_Pi_Zero1.GND
  VCC: Power_plug1.VCC, Dual_MC33926_Motor_Driver_Carrier1.VIN, Dual_MC33926_Motor_Driver_Carrier1.VIN_(5-28)
  VDD: Dual_MC33926_Motor_Driver_Carrier1.VDD, Dual_MC33926_Motor_Driver_Carrier1.SLEW, Dual_MC33926_Motor_Driver_Carrier1.M2_PWM_D2, Dual_MC33926_Motor_Driver_Carrier1.JP6, Dual_MC33926_Motor_Driver_Carrier1.JP9, Teensy_3_1.3V3, R2.Pin_1, R1.Pin_1
  N5: Dual_MC33926_Motor_Driver_Carrier1.M1_IN2, Teensy_3_1.D9
  N6: Dual_MC33926_Motor_Driver_Carrier1.M1_IN1, Teensy_3_1.D10
  N7: Dual_MC33926_Motor_Driver_Carrier1.M1_PWM_D2, Dual_MC33926_Motor_Driver_Carrier1.JP4
  N8: Dual_MC33926_Motor_Driver_Carrier1.M1_SF, Teensy_3_1.D8
  N9: Dual_MC33926_Motor_Driver_Carrier1.M1_FB, Teensy_3_1.A0/D14
  N10: Dual_MC33926_Motor_Driver_Carrier1.EN, Teensy_3_1.D13
  N11: Dual_MC33926_Motor_Driver_Carrier1.M2_IN2, Teensy_3_1.A8/D22
  N12: Dual_MC33926_Motor_Driver_Carrier1.M2_IN1, Teensy_3_1.A9/D23
  N13: Dual_MC33926_Motor_Driver_Carrier1.M2_SF, Teensy_3_1.A6/D20
  N14: Dual_MC33926_Motor_Driver_Carrier1.M2_FB, Teensy_3_1.A1/D15
  N15: Teensy_3_1.A4/D18, Raspberry_Pi_Zero1.GPIO2, R2.Pin_0
  N16: Teensy_3_1.A5/D19, Raspberry_Pi_Zero1.GPIO3, R1.Pin_0

custom parts:
  Pololu #1213 Dual MC33926 Motor Driver Carrier: Dual brushed DC motor driver, based on Freescale’s MC33926 full H-bridge, has a wide operating range of 5 – 28 V and can deliver almost 3 A continuously (5 A peak) to each of its two motor channels. The MC33926 works with 3 – 5 V logic levels, supports ultrasonic (up to 20 kHz) PWM, and features current feedback, under-voltage protection, over-current protection, and over-temperature protection.
