# Fritzing sketch duino-motor-driver (saved by Fritzing 0.9.3b)
breadboards: 1

parts:
  Part1 = Arduino Uno (Rev3)
  M1 = DC Motor
  M2 = DC Motor
  Power_plug1 = Power plug
  Dual_MC33926_Motor_Driver_Carrier1 = Pololu #1213 Dual MC33926 Motor Driver Carrier [package=THT]

nets:
  N1: Part1.A0, Dual_MC33926_Motor_Driver_Carrier1.M1_FB
  N2: Part1.A1, Dual_MC33926_Motor_Driver_Carrier1.M2_FB
  N3: Part1.D8, Dual_MC33926_Motor_Driver_Carrier1.EN
  N4: Part1.D9_PWM, Dual_MC33926_Motor_Driver_Carrier1.M2_IN2
  N5: Part1.D10_PWM/SS, Dual_MC33926_Motor_Driver_Carrier1.M2_IN1
  N6: Part1.D11_PWM/MOSI, Dual_MC33926_Motor_Driver_Carrier1.M2_PWM_D2
  N7: Part1.D12/MISO, Dual_MC33926_Motor_Driver_Carrier1.M2_SF
  GND: Part1.GND, Power_plug1.GND, Dual_MC33926_Motor_Driver_Carrier1.GND, Dual_MC33926_Motor_Driver_Carrier1.M1_PWM_D1, Dual_MC33926_Motor_Driver_Carrier1.M2_PWM_D1, Dual_MC33926_Motor_Driver_Carrier1.JP2, Dual_MC33926_Motor_Driver_Carrier1.JP8
  N8: Part1.D4, Dual_MC33926_Motor_Driver_Carrier1.M1_IN2
  N9: Part1.D5_PWM, Dual_MC33926_Motor_Driver_Carrier1.M1_IN1
  N10: Part1.D6_PWM, Dual_MC33926_Motor_Driver_Carrier1.M1_PWM_D2
  N11: Part1.D7, Dual_MC33926_Motor_Driver_Carrier1.M1_SF
  5V: Part1.5V, Dual_MC33926_Motor_Driver_Carrier1.VDD, Dual_MC33926_Motor_Driver_Carrier1.SLEW, Dual_MC33926_Motor_Driver_Carrier1.JP6
  N12: M1.pin_1, Dual_MC33926_Motor_Driver_Carrier1.M1_OUT2
  N13: M1.pin_2, Dual_MC33926_Motor_Driver_Carrier1.M1_OUT1
  N14: M2.pin_1, Dual_MC33926_Motor_Driver_Carrier1.M2_OUT2
  N15: M2.pin_2, Dual_MC33926_Motor_Driver_Carrier1.M2_OUT1
  VCC: Power_plug1.VCC, Dual_MC33926_Motor_Driver_Carrier1.VIN, Dual_MC33926_Motor_Driver_Carrier1.VIN_(5-28)

custom parts:
  Pololu #1213 Dual MC33926 Motor Driver Carrier: Dual brushed DC motor driver, based on Freescale’s MC33926 full H-bridge, has a wide operating range of 5 – 28 V and can deliver almost 3 A continuously (5 A peak) to each of its two motor channels. The MC33926 works with 3 – 5 V logic levels, supports ultrasonic (up to 20 kHz) PWM, and features current feedback, under-voltage protection, over-current protection, and over-temperature protection.
